# Fritzing sketch Electrical Drawings (saved by Fritzing 0.9.3b)
breadboards: 1

parts:
  Part1 = Arduino Mega ADK (Rev3)
  Left = hc-sr04
  Back = hc-sr04
  Right = hc-sr04
  Down = hc-sr04
  Front = hc-sr04
  Part2 = Bluetooth Mate Silver
  Part3 = Arduino Nano (Rev3.0)
  R3 = Resistor [tolerance=±5% resistance=220 package="0603 [SMD]"]
  LED1 = smd LED [color="Red (633nm)" package="0603 [SMD]"]
  LED2 = smd LED [color="Red (633nm)" package="0603 [SMD]"]
  LED3 = smd LED [color="Red (633nm)" package="0603 [SMD]"]
  LED5 = smd LED [color="Red (633nm)" package="0603 [SMD]"]
  LED6 = smd LED [color="Red (633nm)" package="0603 [SMD]"]
  LED7 = smd LED [color="Red (633nm)" package="0603 [SMD]"]
  R9 = Resistor [tolerance=±5% resistance=220 package="0603 [SMD]"]  # not connected
  R10 = Resistor [tolerance=±5% resistance=220 package="0603 [SMD]"]
  R11 = Resistor [tolerance=±5% resistance=220 package="0603 [SMD]"]
  R12 = Resistor [tolerance=±5% resistance=220 package="0603 [SMD]"]
  R13 = Resistor [tolerance=±5% resistance=220 package="0603 [SMD]"]
  R14 = Resistor [tolerance=±5% resistance=220 package="0603 [SMD]"]
  R15 = Resistor [tolerance=±5% resistance=220 package="0603 [SMD]"]
  LED8 = smd LED [color="Red (633nm)" package="0603 [SMD]"]
  LED9 = smd LED [color="Red (633nm)" package="0603 [SMD]"]
  Part4 = Shift Register Breakout - 74HC595
  Part5 = Compass Module - HMC6352
  BAT1 = Battery Holders [package=battery-aaa]
  SG1 = Buzzer 12mm [package=buzzer-ccv]

nets:
  VCC: Part1.A15, Part1.VIN, Left.VCC, Back.VCC, Right.VCC, Down.VCC, Front.VCC, Part2.VCC, Part3.VIN, Part4.VCC, Part5.VCC, BAT1.-, BAT1.+
  N1: Part1.A0, Part3.A1
  N2: Part1.A1, Part3.A0
  N3: Part1.D21/SCL, Part5.SCL
  N4: Part1.D20/SDA, Part5.SDA
  GND: Part1.GND, Left.GND, Back.GND, Right.GND, Down.GND, Front.GND, Part2.GND, Part3.GND, R3.Pin_1, R10.Pin_1, R11.Pin_1, R12.Pin_1, R13.Pin_1, R14.Pin_1, R15.Pin_1, Part4.GND, Part5.GND, SG1.1
  N5: Part1.D23, SG1.2
  N6: Part1.D28, Part4.LATCH_CLOCK
  N7: Part1.D29, Part4.SERIAL_IN
  N8: Part1.D30, Part4.CLOCK
  N9: Part1.D40, Front.Trig
  N10: Part1.D41, Front.Echo
  N11: Part1.D42, Down.Trig
  N12: Part1.D43, Down.Echo
  N13: Part1.D44, Right.Trig
  N14: Part1.D45, Right.Echo
  N15: Part1.D46, Left.Trig
  N16: Part1.D47, Left.Echo
  N17: Part1.D48, Back.Trig
  N18: Part1.D49, Back.Echo
  N19: Part1.D50/MISO, Part2.RX_5V
  N20: Part1.D51/MOSI, Part2.TX_5V
  N21: R3.Pin_0, LED5.anode
  N22: LED1.cathode, Part4.QE
  N23: LED1.anode, R12.Pin_0
  N24: LED2.cathode, Part4.QF
  N25: LED2.anode, R13.Pin_0
  N26: LED3.cathode, Part4.QD
  N27: LED3.anode, R11.Pin_0
  N28: LED5.cathode, Part4.QA
  N29: LED6.cathode, Part4.QB
  N30: LED7.cathode, Part4.QC
  N31: LED7.anode, R10.Pin_0
  N32: R14.Pin_0, LED9.anode
  N33: R15.Pin_0, LED8.anode
  N34: LED8.cathode, Part4.QG
  N35: LED9.cathode, Part4.QH
